# Fritzing sketch archsound_wiring (saved by Fritzing 0.9.3b)
breadboards: 1

parts:
  Mod1 = Raspberry Pi 4B
  IC1 = MCP3008 8-channel 10-bit ADC [part_number=MCP3008]
  IC2 = MCP3008 8-channel 10-bit ADC [part_number=MCP3008]
  R1 = Rotary Potentiometer (Small) [maximum_resistance=100kΩ package=THT]
  R2 = Rotary Potentiometer (Small) [maximum_resistance=100kΩ package=THT]

nets:
  N1: Mod1.5V, IC1.no_name_yet#15, IC1.no_name_yet#16, IC2.no_name_yet#15, IC2.no_name_yet#16, R1.leg1, R2.leg1
  N2: Mod1.GND, IC1.no_name_yet#9, IC1.no_name_yet#14, IC2.no_name_yet#9, IC2.no_name_yet#14, R1.leg2, R2.leg2
  N3: Mod1.GPIO18, IC2.no_name_yet#10
  N4: Mod1.GPIO10, IC1.no_name_yet#11
  N5: Mod1.GPIO9, IC1.no_name_yet#12
  N6: Mod1.GPIO11, IC1.no_name_yet#13
  N7: Mod1.GPIO8, IC1.no_name_yet#10
  N8: Mod1.GPIO19, IC2.no_name_yet#12
  N9: Mod1.GPIO20, IC2.no_name_yet#11
  N10: Mod1.GPIO21, IC2.no_name_yet#13
  N11: IC1.no_name_yet#1, R1.wiper
  N12: IC2.no_name_yet#1, R2.wiper
